# Fritzing sketch atmega (saved by Fritzing 0.9.6b)
breadboards: 1

parts:
  Motor-2 = female pin header, 2 pins [form="♀ (female)"]  # not connected
  Driver = L293D [package=THT]
  BAT1 = Battery Holders [package=battery-aa-panel]
  U1 = Voltage Regulator - 5V [package="TO220 [THT]"]
  HC-SR04_Sensor_1 = HC-SR04 Ultrasonic Distance Sensor
  HC-SR04_Sensor_2 = HC-SR04 Ultrasonic Distance Sensor
  HC-SR04_Sensor_3 = HC-SR04 Ultrasonic Distance Sensor
  C1 = Ceramic Capacitor [capacitance=22pF voltage=35V package="100 mil [THT, multilayer]"]
  C2 = Ceramic Capacitor [capacitance=22pF voltage=35V package="100 mil [THT, multilayer]"]
  R2 = Resistor [tolerance=±5% power=0.25 resistance=1000 package=THT]
  Y1 = Resonator [frequency="16 Mhz" package=THT]
  Atmega = atmega328 [package=dip]
  M1 = DC Motor
  M2 = DC Motor

nets:
  N1: Driver.Enable_1, Driver.Enable_2, Atmega.D3_(PWM)
  N2: Driver.In_1, Atmega.D4
  N3: Driver.Out_1_(_Controlled_by_Enable_1_), M2.pin_1
  GND: Driver.0V, BAT1.-, U1.GND, HC-SR04_Sensor_1.GND, HC-SR04_Sensor_2.GND, HC-SR04_Sensor_3.GND, C1.1, C2.1, Atmega.GND
  N4: Driver.Out_2_(_Controlled_by_Enable_1_), M2.pin_2
  N5: Driver.In_2, Atmega.D2
  VCC: Driver.+Vmotor, Driver.+V, U1.output_voltage, HC-SR04_Sensor_1.VCC, HC-SR04_Sensor_2.VCC, HC-SR04_Sensor_3.VCC, R2.Pin_1, Atmega.VCC, Atmega.AVCC
  N6: Driver.In_3, Atmega.D0_(RX)
  N7: Driver.Out_3_(_Controlled_by_Enable_2_), M1.pin_2
  N8: Driver.Out_4_(_Controlled_by_Enable_2_), M1.pin_1
  N9: Driver.In_4, Atmega.D1_(TX)
  N10: BAT1.+, U1.input_voltage
  N11: HC-SR04_Sensor_1.TRIG, HC-SR04_Sensor_2.TRIG, HC-SR04_Sensor_3.TRIG, Atmega.D7
  N12: HC-SR04_Sensor_1.ECHO, Atmega.D9_(PWM)
  N13: HC-SR04_Sensor_2.ECHO, Atmega.D5_(PWM)
  N14: HC-SR04_Sensor_3.ECHO, Atmega.D6_(PWM)
  N15: C1.0, Y1.1, Atmega.XLAT2
  N16: C2.0, Y1.0, Atmega.XLAT1
  N17: R2.Pin_0, Atmega.RESET
