# Fritzing sketch obstacle-avoider (saved by Fritzing 0.9.6b)
breadboards: 1

parts:
  Part1 = Arduino Uno (Rev3)
  IC1 = L293D [package=THT]
  HC-SR04_Sensor_1 = HC-SR04 Ultrasonic Distance Sensor
  R1 = Resistor [tolerance=±5% power=0.25 resistance=330 package=THT]
  LED1 = LED - 5mm [color="Red (633nm)" current=0.030 package="5 mm [THT]"]
  LED2 = LED - 5mm [color="Green (555nm)" current=0.030 package="5 mm [THT]"]
  R2 = Resistor [tolerance=±5% power=0.25 resistance=330 package=THT]
  LED3 = LED - 5mm [color="Green (555nm)" current=0.030 package="5 mm [THT]"]
  LED4 = LED - 5mm [color="Red (633nm)" current=0.030 package="5 mm [THT]"]

nets:
  GND: Part1.GND, IC1.0V, HC-SR04_Sensor_1.GND
  N1: Part1.D0/RX, IC1.In_2
  N2: Part1.D1/TX, IC1.In_1
  N3: Part1.D4, IC1.In_3
  N4: Part1.D5_PWM, IC1.In_4
  5V: Part1.5V, IC1.Enable_1, IC1.+Vmotor, IC1.Enable_2, IC1.+V, HC-SR04_Sensor_1.VCC
  N5: IC1.Out_1_(_Controlled_by_Enable_1_), LED1.anode, LED2.cathode
  N6: IC1.Out_2_(_Controlled_by_Enable_1_), R1.Pin_1
  N7: IC1.Out_3_(_Controlled_by_Enable_2_), LED3.cathode, LED4.anode
  N8: IC1.Out_4_(_Controlled_by_Enable_2_), R2.Pin_1
  N9: R1.Pin_0, LED1.cathode, LED2.anode
  N10: R2.Pin_0, LED3.anode, LED4.cathode
